# Fritzing sketch projetoDetectorSalAcucarComSupervisorio (saved by Fritzing 0.9.4)
circuit board: 8.46667cm x 5.64444cm
breadboards: 2

parts:
  Arduino_UNO = Arduino Uno (Rev3)
  INA219 = INA219 High Side DC Current Sensor Breakout [part_number=904]
  Recipiente_com_solução_aquosa = Battery Holders [package=battery-aa-kit]
  R1 = Resistor [tolerance=±5% resistance=10k package="0805 [SMD]"]
  R2 = Resistor [tolerance=±5% resistance=1k package="2010 [SMD]"]
  R3 = Resistor [tolerance=±5% resistance=1k package="2010 [SMD]"]
  R4 = Resistor [tolerance=±5% resistance=1k package="2010 [SMD]"]
  R6 = Resistor [tolerance=±5% resistance=1k package="2010 [SMD]"]
  R7 = Resistor [tolerance=±5% resistance=1k package="2010 [SMD]"]
  LED1 = LED - 3mm [color="Red (633nm)" package="3 mm [THT]"]
  LED2 = LED - 3mm [color="Yellow (574nm)" package="3 mm [THT]"]
  LED3 = LED - 3mm [color="Green (565nm)" package="3 mm [THT]"]
  R5 = Resistor [tolerance=±5% resistance=1k package="2010 [SMD]"]
  U1 = Quad Comparator [part_number=LM239 package="DIP (Dual Inline) [THT]"]
  part = LM239 [part_number=LM239]  # not connected
  U1_1 = LM239 [part_number=LM239]  # not connected
  U1_3 = LM239 [part_number=LM239]  # not connected
  U1_4 = LM239 [part_number=LM239]  # not connected

nets (from the pcb view):
  N1: Arduino_UNO.A4/SDA, INA219.SDA
  N2: Arduino_UNO.A5/SCL, INA219.SCL
  5V: Arduino_UNO.5V, INA219.VCC
  GND: Arduino_UNO.GND, INA219.GND, R5.Pin_0, U1.connector5
  N3: INA219.VIN-, Recipiente_com_solução_aquosa.-
  N4: INA219.VIN+, R1.Pin_0
  N5: Recipiente_com_solução_aquosa.+, R1.Pin_1
  N6: R2.Pin_0, R3.Pin_1, U1.connector7
  N7: R2.Pin_1, R4.Pin_1, R6.Pin_1, R7.Pin_1, U1.connector11
  N8: R3.Pin_0, R5.Pin_1, U1.connector9
  N9: R4.Pin_0, LED1.cathode
  N10: R6.Pin_0, LED3.cathode
  N11: R7.Pin_0, LED2.cathode
  N12: LED1.anode, U1.connector0
  N13: LED2.anode, U1.connector12
  N14: LED3.anode, U1.connector13
  N15: U1.connector6, U1.connector8, U1.connector10

custom parts:
  INA219 High Side DC Current Sensor Breakout: This breakout board will solve all your power-monitoring problems. Instead of struggling with two multimeters, you can just use the handy INA219B chip on this breakout to both measure both the high side voltage and DC current draw over I2C with 1% precision. Most current-measuring devices such as our current panel meter are only good for low side measuring. That means that unless you want to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

// code stored in the sketch: detectorSalAcucar.ino

#include <Adafruit_INA219.h>        // biblioteca ina219 
 
const int INA_addr = 0x40;  // endereço INA219 
 
// indica o endereço do INA219 - 0x40
Adafruit_INA219 ina219(INA_addr);
 
float shuntvoltage = 0;
float current_mA = 0;

// pino para saida digital com valor da referência
int pinoDigital = 9;
 
// protótipo das funções
void Read_INA219_Values(void);
void Serial_Send(void);
 
void setup()
{
  // configura o serial com 9600bps
  Serial.begin(9600);

 // configura o pino como saida
	pinMode(pinoDigital, OUTPUT);

 // inicializa o INA219
  ina219.begin();
}
 
void loop()
{

  // recebe um valor de 0 a 255
  analogWrite(pinoDigital,128);
  
  // lê os valores do INA219
  Read_INA219_Values();
 
  // envia os dados pela serial
  Serial_Send();
 
	//espera 1000ms
  delay(1000);
}
 
// l? os valores convertidos pelo modulo INA219
void Read_INA219_Values(void)
{
	//lê a tensão entre V- e V+
  shuntvoltage = ina219.getShuntVoltage_mV();

	//lê a corrente 
  current_mA = ina219.getCurrent_mA();
  
}
 

// envia os valores pela serial
void Serial_Send(void)
{
  Serial.print("V/"); Serial.println(shuntvoltage);
  Serial.print("C/"); Serial.println(current_mA);
}
